// Logisim project mux.circ as structural Verilog: 2 circuits, main circuit main
module main (
  input  in_1,
  input  in_2,
  input  in_3,
  input  in_4,
  input  in_5,
  input  in_6,
  output out_7
);

  multiplex multiplex_1 (.D0(in_3), .D1(in_4), .D2(in_5), .D3(in_6), .Y(out_7), .S0(in_1), .S1(in_2));
endmodule

module multiplex (
  input  S0,
  input  S1,
  input  D0,
  input  D1,
  input  D2,
  input  D3,
  output Y
);

  wire and_1_out, and_2_out, and_3_out, and_4_out, not_1_out, not_2_out;

  not not_1 (not_1_out, S0);
  not not_2 (not_2_out, S1);
  and and_1 (and_1_out, not_2_out, not_1_out, D0);
  and and_2 (and_2_out, D1, not_2_out, S0);
  and and_3 (and_3_out, D2, S1, not_1_out);
  and and_4 (and_4_out, D3, S0, S1);
  or or_1 (Y, and_1_out, and_2_out, and_3_out, and_4_out);
endmodule
